# Fritzing sketch mushroom_circuit (saved by Fritzing 0.9.5d)

parts:
  WeMos_D1_Mini1 = WeMos D1 Mini
  Part1 = NeoPixel Stick [part_number=1426]
  Part2 = NeoPixel Stick [part_number=1426]
  ENCODER1 = Rotary Encoder with Knob
  TP1 = TP4056 [chip_label=TP4056 package="DIP (Dual Inline) [THT]"]
  Bat1 = battery_holder_dual_18650 [part_number=TBH-18650-2A-P]
  Q1 = Basic FET N-Channel [package="TO220 [THT]"]

nets:
  +5V: WeMos_D1_Mini1.5V, Part1.+5V, Part2.+5V, TP1.pin3
  N1: WeMos_D1_Mini1.D3, Part1.DATAIN
  N2: WeMos_D1_Mini1.D4, Q1.gate
  N3: WeMos_D1_Mini1.D5, ENCODER1.no_name_yet#3
  N4: WeMos_D1_Mini1.D6, ENCODER1.no_name_yet#4
  N5: WeMos_D1_Mini1.D7, ENCODER1.no_name_yet#1
  N6: WeMos_D1_Mini1.G, ENCODER1.no_name_yet#2, ENCODER1.no_name_yet#5
  GND: Part1.GND, Part2.GND, Q1.source
  N7: Part1.DATAOUT, Part2.DATAIN
  N8: TP1.pin4, Bat1.+#2
  N9: TP1.pin5, Bat1.+#1
  N10: TP1.pin6, Q1.drain

custom parts:
  NeoPixel Stick: Make your own little LED strip arrangement with this stick of NeoPixel LEDs. We crammed 8 of the tiny 5050 (5mm x 5mm) smart RGB LEDs onto a PCB with mounting holes and a chainable design. Use only one microcontroller pin to control as many as you can chain together! Each LED is addressable as the driver chip is inside the LED. Each one has ~18mA constant current drive so the color will be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
  Rotary Encoder with Knob: Rotary Encoder with 1/4" Shaft and Knob
  TP4056: A DIP stand-in part for whatever IC you want. With 6 pins on a 300mil dual inline package (DIP) footprint.
  battery_holder_dual_18650: TBH-18650-2A-P dual 18650 battery holder.
